# Fritzing sketch Clase 6 (Sensor de Temperatura DHT11) (saved by Fritzing 0.9.3b)
breadboards: 1

parts:
  Mod1 = KY-015 Temperature & Humidity Sensor Module [package="Breakout board"]
  Componente1 = Arduino Uno (Rev3)
  R1 = Resistor [tolerance=±5% resistance=220 package=THT]
  LED1 = LED - 5mm [color="Red (633nm)" package="5 mm [THT]"]

nets:
  N1: Mod1.S, Componente1.D5_PWM
  VIN: Mod1.Vin, Componente1.5V
  N2: Mod1.-, Componente1.GND, LED1.cathode
  N3: Componente1.D13/SCK, R1.Pin_1
  N4: R1.Pin_0, LED1.anode

custom parts:
  KY-015 Temperature & Humidity Sensor Module: KY-015 temperature and humidity sensor module, provides a low-latency serial interface to measure humidity and temperature.
