# Fritzing sketch Clase 10 Sensor PIR HC-SR501 (saved by Fritzing 0.9.3b)
breadboards: 1

parts:
  PIR1 = PIR sensor
  Componente1 = Arduino Pro Micro (Clone)
  R1 = Resistor [tolerance=±5% resistance=100 package=THT]
  LED1 = LED - 5mm [color="Red (633nm)" package="5 mm [THT]"]

nets:
  VDD: PIR1.VDD, Componente1.VCC
  N1: PIR1.SIG, Componente1.D2
  GND: PIR1.GND, Componente1.GND, R1.Pin_0
  N2: Componente1.D5, LED1.anode
  N3: R1.Pin_1, LED1.cathode
