# Fritzing sketch Clase 3 (Entradas PWM) (saved by Fritzing 0.9.3b)
breadboards: 1

parts:
  Componente1 = Arduino Uno (Rev3)
  R1 = Rotary Potentiometer (Small) [maximum_resistance=100kΩ package=THT]
  LED1 = LED - 5mm [color="Red (633nm)" package="5 mm [THT]"]
  R2 = Resistor [tolerance=±5% resistance=330 package=THT]  # not connected

nets:
  N1: Componente1.A0, R1.wiper
  N2: Componente1.D9_PWM, LED1.anode
  N3: Componente1.GND, R1.leg1
  N4: Componente1.5V, R1.leg2
