# Fritzing sketch Clase 5 (Ultrasonico) (saved by Fritzing 0.9.3b)
breadboards: 1

parts:
  Componente1 = Arduino Uno (Rev3)
  Componente2 = HC-SR04

nets:
  N1: Componente1.D8, Componente2.Trig
  N2: Componente1.D9_PWM, Componente2.Echo
  5V: Componente1.5V, Componente2.Vcc

custom parts:
  HC-SR04: HC-SR04 ultrasonic distance sensor
