# Fritzing sketch Clase 4 (Pulsadores) (saved by Fritzing 0.9.3b)
breadboards: 1

parts:
  S1 = Pushbutton [package="[THT]"]
  S2 = Pushbutton [package="[THT]"]
  R1 = Resistor [tolerance=±5% power=0.25 resistance=220 package=THT]
  R2 = Resistor [tolerance=±5% power=0.25 resistance=220 package=THT]
  R3 = Resistor [tolerance=±5% power=0.25 resistance=220 package=THT]
  Part1 = Arduino Uno (Rev3)
  LED1 = LED - 5mm [color="Blue (430nm)" current=0.030 package="5 mm [THT]"]
  LED2 = LED - 5mm [color="Green (565nm)" current=0.030 package="5 mm [THT]"]
  LED3 = LED - 5mm [color="Red (633nm)" current=0.030 package="5 mm [THT]"]
  R4 = Resistor [tolerance=±5% power=0.25 resistance=10k package=THT]

nets:
  N1: S1.Pin_1, S1.Pin_2, Part1.D8, R4.Pin_0
  N2: S1.Pin_3, S1.Pin_4, Part1.5V
  N3: S2.Pin_1, S2.Pin_2, Part1.D9_PWM
  N4: S2.Pin_3, S2.Pin_4, R1.Pin_0, R2.Pin_0, R3.Pin_0, Part1.GND, R4.Pin_1
  N5: R1.Pin_1, LED3.cathode
  N6: R2.Pin_1, LED2.cathode
  N7: R3.Pin_1, LED1.cathode
  N8: Part1.D3_PWM, LED2.anode
  N9: Part1.D4, LED1.anode
  N10: Part1.D5_PWM, LED3.anode
